# Fritzing sketch TFT_1x3in_240x240_connections (saved by Fritzing 0.9.3b)

parts:
  J11 = female pin header, 8 pins [form="♀ (female)"]
  J12 = female pin header, 11 pins [form="♀ (female)"]

nets:
  N1: J11.pin1, J12.pin3
  N2: J11.pin2, J12.pin1
  N3: J11.pin3, J12.pin8
  N4: J11.pin4, J12.pin9
  N5: J11.pin5, J12.pin7
  N6: J11.pin6, J12.pin6
  N7: J11.pin7, J12.pin4
  N8: J11.pin8, J12.pin11

notes:
  TFT Connections (left to right from BACK)
  Red: Vin 3-5 ok
  (skip): 3.3v out from board
  Black: Ground
  Orange: SCLK (SPI clock)
  (skip): MISO
  White: MOSI (master out Slave In)
  Yellow: TFT CS
  Blue: Reset (gnd = reset)
  Green: D/C (data/command)
  (skip): Card CS
  Red: Lite (can PWM or +3-5 or
  leave open)
  Standard 8 pin header connections
  Black: Ground
  Red: Vcc 3-5 ok
  Blue: Reset (gnd = reset) (Itsy D9)
  Green: D/C (data/command) (Itsy D7)
  Yellow: TFT CS (Itsy D10)
  White: MOSI (master out Slave In) (MOSI)
  Orange: SCLK (SPI clock) (SCK)
  Red: Lite (power 3-5 v)
  1.3 or 1.54 in 240x240 TFT
  also 1.14 in 240x135 TFT
  permaproto header
  (gnd) ... (lite)
  TFT (back)
  (Vin) ... (lite)
