# Fritzing sketch TFT_1x8in_connections (saved by Fritzing 0.9.3b)

parts:
  J11 = female pin header, 8 pins [form="♀ (female)" part_number="8 pin header"]
  Part3 = TFT 1.8 inch 160x128 w microSD [part_number=358]

nets:
  N1: J11.pin1, Part3.GND
  N2: J11.pin2, Part3.+5V
  N3: J11.pin3, Part3.RESET
  N4: J11.pin4, Part3.CARDCS, Part3.TFTDC
  N5: J11.pin5, Part3.TFTCS
  N6: J11.pin6, Part3.MOSI
  N7: J11.pin7, Part3.SCLK
  N8: J11.pin8, Part3.LITE

notes:
  TFT Connections (left to right)
  Black: Ground
  Red: Vcc 3-5 ok
  Blue: Reset (gnd = reset)
  Green: D/C (data/command)
  (skip): Card CS
  Yellow: TFT CS
  White: MOSI (master out Slave In)
  Orange: SCLK (SPI clock)
  (skip): MISO
  Red: Lite (power 3-5 v)
  Standard 8 pin header connections
  Black: Ground
  Red: Vcc 3-5 ok
  Blue: Reset (gnd = reset) (Itsy D9)
  Green: D/C (data/command) (Itsy D7)
  Yellow: TFT CS (Itsy D10)
  White: MOSI (master out Slave In) (MOSI)
  Orange: SCLK (SPI clock) (SCK)
  Red: Lite (power 3-5 v)
  1.8 in 160x128 TFT
  permaproto header
  (gnd) ... (lite)

custom parts:
  TFT 1.8 inch 160x128 w microSD: This lovely little display breakout is the best way to add a small, colorful and bright display to any project. Since the display uses 4-wire SPI to communicate and has its own pixel-addressable frame buffer, it can be used with every kind of microcontroller. Even a very small one with low memory and few pins available! The 1.8" display has 128x160 color pixels.
